// Logisim project MatrixCalculation.circ as structural Verilog: 1 circuit, main circuit MAC
module MAC (
  input  [31:0] A,
  input  [31:0] X,
  input  [31:0] B,
  input  clock,
  output [31:0] Result,
  output Done
);


  // Other names for the same wires on the sheet: A_1_1[7:0] = A[7:0]; A_1_2[7:0] = A[15:8]; A_2_1[7:0] = A[23:16];
  //   A_2_2[7:0] = A[31:24]; B_1_1[7:0] = B[7:0]; B_1_2[7:0] = B[15:8]; B_2_1[7:0] = B[23:16]; B_2_2[7:0] = B[31:24];
  //   clk = clock; Result_1_1[7:0] = Result[7:0]; Result_1_2[7:0] = Result[15:8]; Result_2_1[7:0] = Result[23:16];
  //   Result_2_2[7:0] = Result[31:24]; X_1_1[7:0] = X[7:0]; X_1_2[7:0] = X[15:8]; X_2_1[7:0] = X[23:16];
  //   X_2_2[7:0] = X[31:24]

  // Notes on the sheet:
  //   Please don't change places of inputs and outputs
endmodule
